// Logisim project p1.circ as structural Verilog: 1 circuit, main circuit main
module main (
  input  in_1,
  input  in_2,
  output out_3
);

  wire transistor_2_out;

  Transistor #(.\type ("n")) transistor_1 (.in(1'b0), .out(out_3), .gate(in_1));
  Transistor transistor_2 (.in(1'b1), .out(transistor_2_out), .gate(in_1));
  Transistor transistor_3 (.in(transistor_2_out), .out(out_3), .gate(in_2));
  Transistor #(.\type ("n")) transistor_4 (.in(1'b0), .out(out_3), .gate(in_2));
  Transistor transistor_5 ();  // open: in, out, gate
  Transistor transistor_6 ();  // open: in, out, gate
  Transistor #(.\type ("n")) transistor_7 ();  // open: in, out, gate
  Transistor #(.\type ("n")) transistor_8 ();  // open: in, out, gate
endmodule
