// Logisim project p1.circ as structural Verilog: 2 circuits, main circuit main
module main (
  input  Inputs,
  input  in_2,
  input  in_3,
  input  in_4,
  input  in_5,
  input  Clock,
  output Outputs,
  output out_8,
  output out_9,
  output out_10,
  output out_11
);

  Register #(.width(1)) register_1 (.D(Inputs), .en(1'b1), .Q(Outputs), .clk(Clock));  // open: clr
  Register #(.width(1)) register_2 (.D(in_2), .en(1'b1), .Q(out_8), .clk(Clock));  // open: clr
  Register #(.width(1)) register_3 (.D(in_3), .en(1'b1), .Q(out_9), .clk(Clock));  // open: clr
  Register #(.width(1)) register_4 (.D(in_4), .en(1'b1), .Q(out_10), .clk(Clock));  // open: clr
  Register #(.width(1)) register_5 (.D(in_5), .en(1'b1), .Q(out_11), .clk(Clock));  // open: clr

  // Notes on the sheet:
  //   Enable
  //   ADARSH CHAUDHARY    (1701CS01)
endmodule

module p1 (
  input  in_1,
  input  in_2,
  input  in_3,
  input  in_4,
  input  in_5,
  output out_6,
  output out_7,
  output out_8,
  output out_9,
  output out_10,
  output out_11,
  output out_12,
  output out_13,
  output out_14,
  output out_15,
  output out_16,
  output out_17,
  output out_18,
  output out_19,
  output out_20
);

  wire clock_1_out;

  Clock clock_1 (.out(clock_1_out));
  main main_1 (
    .Inputs(in_1), .in_2(in_2), .in_3(in_3), .in_4(in_4), .in_5(in_5), .Clock(clock_1_out), .Outputs(out_6),
    .out_8(out_7), .out_9(out_8), .out_10(out_9), .out_11(out_10));
  main main_2 (
    .Inputs(out_6), .in_2(out_7), .in_3(out_8), .in_4(out_9), .in_5(out_10), .Clock(clock_1_out),
    .Outputs(out_11), .out_8(out_12), .out_9(out_13), .out_10(out_14), .out_11(out_15));
  main main_3 (
    .Inputs(out_11), .in_2(out_12), .in_3(out_13), .in_4(out_14), .in_5(out_15), .Clock(clock_1_out),
    .Outputs(out_16), .out_8(out_17), .out_9(out_18), .out_10(out_19), .out_11(out_20));

  // Notes on the sheet:
  //   ADARSH CHAUDHARY    (1701CS01)
endmodule
