// Logisim project p2.circ as structural Verilog: 1 circuit, main circuit main
module main (
  input  in_1,
  input  in_2,
  output out_3,
  output out_4,
  output out_5,
  output out_6
);

  wire clock_1_out, multiplexer_1_out, multiplexer_2_out, multiplexer_3_out, multiplexer_4_out;

  Clock clock_1 (.out(clock_1_out));
  Multiplexer #(.enable("false")) multiplexer_1 (.in0(out_3), .in1(in_1), .out(multiplexer_1_out), .sel(in_2));
  Register #(.width(1)) register_1 (.D(multiplexer_1_out), .en(1'b1), .Q(out_3), .clk(clock_1_out));  // open: clr
  Multiplexer #(.enable("false")) multiplexer_2 (.in0(out_4), .in1(out_3), .out(multiplexer_2_out), .sel(in_2));
  Register #(.width(1)) register_2 (.D(multiplexer_2_out), .en(1'b1), .Q(out_4), .clk(clock_1_out));  // open: clr
  Multiplexer #(.enable("false")) multiplexer_3 (.in0(out_5), .in1(out_4), .out(multiplexer_3_out), .sel(in_2));
  Register #(.width(1)) register_3 (.D(multiplexer_3_out), .en(1'b1), .Q(out_5), .clk(clock_1_out));  // open: clr
  Multiplexer #(.enable("false")) multiplexer_4 (.in0(out_6), .in1(out_5), .out(multiplexer_4_out), .sel(in_2));
  Register #(.width(1)) register_4 (.D(multiplexer_4_out), .en(1'b1), .Q(out_6), .clk(clock_1_out));  // open: clr

  // Notes on the sheet:
  //   ADARSH CHAUDHARY    (1701CS01)
endmodule
