// Logisim project p3.circ as structural Verilog: 1 circuit, main circuit main
module main (
  input  [4:0] Read_0,
  input  [4:0] Read_1,
  input  [31:0] write_value,
  input  [4:0] write_addr,
  input  clock,
  input  clear,
  output [31:0] v0,
  output [31:0] Value_0,
  output [31:0] Value_1
);

  wire decoder_1_out1, decoder_1_out2, decoder_1_out3, decoder_1_out4, decoder_1_out5, decoder_1_out6,
       decoder_1_out7, decoder_1_out8, decoder_1_out9, decoder_1_out10, decoder_1_out11, decoder_1_out12,
       decoder_1_out13, decoder_1_out14, decoder_1_out15, decoder_1_out16, decoder_1_out17, decoder_1_out18,
       decoder_1_out19, decoder_1_out20, decoder_1_out21, decoder_1_out22, decoder_1_out23, decoder_1_out24,
       decoder_1_out25, decoder_1_out26, decoder_1_out27, decoder_1_out28, decoder_1_out29, decoder_1_out30,
       decoder_1_out31;
  wire [31:0] r1_q, r3_q, r4_q, r5_q, r6_q, r7_q, r8_q, r9_q, r10_q, r11_q, r12_q, r13_q, r14_q, r15_q,
       r16_q, r17_q, r18_q, r19_q, r20_q, r21_q, r22_q, r23_q, r24_q, r25_q, r26_q, r27_q, r28_q, r29_q,
       r30_q, r31_q;

  Decoder #(.select(5), .enable("false")) decoder_1 (
    .out1(decoder_1_out1), .out2(decoder_1_out2), .out3(decoder_1_out3), .out4(decoder_1_out4),
    .out5(decoder_1_out5), .out6(decoder_1_out6), .out7(decoder_1_out7), .out8(decoder_1_out8),
    .out9(decoder_1_out9), .out10(decoder_1_out10), .out11(decoder_1_out11), .out12(decoder_1_out12),
    .out13(decoder_1_out13), .out14(decoder_1_out14), .out15(decoder_1_out15), .out16(decoder_1_out16),
    .out17(decoder_1_out17), .out18(decoder_1_out18), .out19(decoder_1_out19), .out20(decoder_1_out20),
    .out21(decoder_1_out21), .out22(decoder_1_out22), .out23(decoder_1_out23), .out24(decoder_1_out24),
    .out25(decoder_1_out25), .out26(decoder_1_out26), .out27(decoder_1_out27), .out28(decoder_1_out28),
    .out29(decoder_1_out29), .out30(decoder_1_out30), .out31(decoder_1_out31), .sel(write_addr));  // open: out0
  Register #(.width(32)) r1 (.D(write_value), .en(decoder_1_out1), .Q(r1_q), .clk(clock), .clr(clear));
  Register #(.width(32)) r2 (.D(write_value), .en(decoder_1_out2), .Q(v0), .clk(clock), .clr(clear));
  Register #(.width(32)) r3 (.D(write_value), .en(decoder_1_out3), .Q(r3_q), .clk(clock), .clr(clear));
  Register #(.width(32)) r4 (.D(write_value), .en(decoder_1_out4), .Q(r4_q), .clk(clock), .clr(clear));
  Register #(.width(32)) r5 (.D(write_value), .en(decoder_1_out5), .Q(r5_q), .clk(clock), .clr(clear));
  Register #(.width(32)) r6 (.D(write_value), .en(decoder_1_out6), .Q(r6_q), .clk(clock), .clr(clear));
  Register #(.width(32)) r7 (.D(write_value), .en(decoder_1_out7), .Q(r7_q), .clk(clock), .clr(clear));
  Register #(.width(32)) r8 (.D(write_value), .en(decoder_1_out8), .Q(r8_q), .clk(clock), .clr(clear));
  Register #(.width(32)) r9 (.D(write_value), .en(decoder_1_out9), .Q(r9_q), .clk(clock), .clr(clear));
  Register #(.width(32)) r10 (.D(write_value), .en(decoder_1_out10), .Q(r10_q), .clk(clock), .clr(clear));
  Register #(.width(32)) r11 (.D(write_value), .en(decoder_1_out11), .Q(r11_q), .clk(clock), .clr(clear));
  Register #(.width(32)) r12 (.D(write_value), .en(decoder_1_out12), .Q(r12_q), .clk(clock), .clr(clear));
  Register #(.width(32)) r13 (.D(write_value), .en(decoder_1_out13), .Q(r13_q), .clk(clock), .clr(clear));
  Register #(.width(32)) r14 (.D(write_value), .en(decoder_1_out14), .Q(r14_q), .clk(clock), .clr(clear));
  Register #(.width(32)) r15 (.D(write_value), .en(decoder_1_out15), .Q(r15_q), .clk(clock), .clr(clear));
  Register #(.width(32)) r16 (.D(write_value), .en(decoder_1_out16), .Q(r16_q), .clk(clock), .clr(clear));
  Register #(.width(32)) r17 (.D(write_value), .en(decoder_1_out17), .Q(r17_q), .clk(clock), .clr(clear));
  Register #(.width(32)) r18 (.D(write_value), .en(decoder_1_out18), .Q(r18_q), .clk(clock), .clr(clear));
  Register #(.width(32)) r19 (.D(write_value), .en(decoder_1_out19), .Q(r19_q), .clk(clock), .clr(clear));
  Register #(.width(32)) r20 (.D(write_value), .en(decoder_1_out20), .Q(r20_q), .clk(clock), .clr(clear));
  Register #(.width(32)) r21 (.D(write_value), .en(decoder_1_out21), .Q(r21_q), .clk(clock), .clr(clear));
  Register #(.width(32)) r22 (.D(write_value), .en(decoder_1_out22), .Q(r22_q), .clk(clock), .clr(clear));
  Register #(.width(32)) r23 (.D(write_value), .en(decoder_1_out23), .Q(r23_q), .clk(clock), .clr(clear));
  Register #(.width(32)) r24 (.D(write_value), .en(decoder_1_out24), .Q(r24_q), .clk(clock), .clr(clear));
  Register #(.width(32)) r25 (.D(write_value), .en(decoder_1_out25), .Q(r25_q), .clk(clock), .clr(clear));
  Register #(.width(32)) r26 (.D(write_value), .en(decoder_1_out26), .Q(r26_q), .clk(clock), .clr(clear));
  Register #(.width(32)) r27 (.D(write_value), .en(decoder_1_out27), .Q(r27_q), .clk(clock), .clr(clear));
  Register #(.width(32)) r28 (.D(write_value), .en(decoder_1_out28), .Q(r28_q), .clk(clock), .clr(clear));
  Register #(.width(32)) r29 (.D(write_value), .en(decoder_1_out29), .Q(r29_q), .clk(clock), .clr(clear));
  Register #(.width(32)) r30 (.D(write_value), .en(decoder_1_out30), .Q(r30_q), .clk(clock), .clr(clear));
  Register #(.width(32)) r31 (.D(write_value), .en(decoder_1_out31), .Q(r31_q), .clk(clock), .clr(clear));
  Multiplexer #(.select(5), .width(32)) multiplexer_1 (
    .in0({32{1'b0}}), .in1(r1_q), .in2(v0), .in3(r3_q), .in4(r4_q), .in5(r5_q), .in6(r6_q), .in7(r7_q),
    .in8(r8_q), .in9(r9_q), .in10(r10_q), .in11(r11_q), .in12(r12_q), .in13(r13_q), .in14(r14_q),
    .in15(r15_q), .in16(r16_q), .in17(r17_q), .in18(r18_q), .in19(r19_q), .in20(r20_q), .in21(r21_q),
    .in22(r22_q), .in23(r23_q), .in24(r24_q), .in25(r25_q), .in26(r26_q), .in27(r27_q), .in28(r28_q),
    .in29(r29_q), .in30(r30_q), .in31(r31_q), .out(Value_0), .sel(Read_0));  // open: en
  Multiplexer #(.select(5), .width(32)) multiplexer_2 (
    .in0({32{1'b0}}), .in1(r1_q), .in2(v0), .in3(r3_q), .in4(r4_q), .in5(r5_q), .in6(r6_q), .in7(r7_q),
    .in8(r8_q), .in9(r9_q), .in10(r10_q), .in11(r11_q), .in12(r12_q), .in13(r13_q), .in14(r14_q),
    .in15(r15_q), .in16(r16_q), .in17(r17_q), .in18(r18_q), .in19(r19_q), .in20(r20_q), .in21(r21_q),
    .in22(r22_q), .in23(r23_q), .in24(r24_q), .in25(r25_q), .in26(r26_q), .in27(r27_q), .in28(r28_q),
    .in29(r29_q), .in30(r30_q), .in31(r31_q), .out(Value_1), .sel(Read_1));  // open: en

  // Notes on the sheet:
  //   ADARSH CHAUDHARY    (1701CS01)
endmodule
