// Logisim project p5.circ as structural Verilog: 2 circuits, main circuit main
module main (
  input  [3:0] Value_A_Selector,
  input  [3:0] Value_B_Selector,
  input  in_3,
  input  [15:0] Input_Value,
  input  [3:0] Selector,
  output [15:0] Value_A,
  output [15:0] Value_B,
  output [15:0] Output
);

  wire clock_1_out;

  Clock clock_1 (.out(clock_1_out));
  register register_1 (
    .Read_0(Value_B_Selector), .Read_1(Value_A_Selector), .write_value(Input_Value), .write_addr(Selector),
    .Value_0(Value_B), .Value_1(Value_A), .clock(clock_1_out), .clear(in_3));
  Adder #(.width(16)) adder_1 (.a(Value_B), .b(Value_A), .out(Output));  // open: cin, cout

  // Notes on the sheet:
  //   ADARSH CHAUDHARY    (1701CS01)
endmodule

module register (
  input  [3:0] Read_0,
  input  [3:0] Read_1,
  input  [15:0] write_value,
  input  [3:0] write_addr,
  input  clock,
  input  clear,
  output [15:0] Value_0,
  output [15:0] Value_1
);

  wire decoder_1_out1, decoder_1_out2, decoder_1_out3, decoder_1_out4, decoder_1_out5, decoder_1_out6,
       decoder_1_out7, decoder_1_out8, decoder_1_out9, decoder_1_out10, decoder_1_out11, decoder_1_out12,
       decoder_1_out13, decoder_1_out14, decoder_1_out15;
  wire [15:0] s0_q, s1_q, s2_q, s3_q, s4_q, s5_q, s6_q, s7_q, t1_q, t2_q, t3_q, t4_q, t5_q, t6_q, t7_q;

  Decoder #(.select(4), .enable("false")) decoder_1 (
    .out1(decoder_1_out1), .out2(decoder_1_out2), .out3(decoder_1_out3), .out4(decoder_1_out4),
    .out5(decoder_1_out5), .out6(decoder_1_out6), .out7(decoder_1_out7), .out8(decoder_1_out8),
    .out9(decoder_1_out9), .out10(decoder_1_out10), .out11(decoder_1_out11), .out12(decoder_1_out12),
    .out13(decoder_1_out13), .out14(decoder_1_out14), .out15(decoder_1_out15), .sel(write_addr));  // open: out0
  Register #(.width(16)) t2 (.D(write_value), .en(decoder_1_out2), .Q(t2_q), .clk(clock), .clr(clear));
  Register #(.width(16)) t4 (.D(write_value), .en(decoder_1_out4), .Q(t4_q), .clk(clock), .clr(clear));
  Register #(.width(16)) t6 (.D(write_value), .en(decoder_1_out6), .Q(t6_q), .clk(clock), .clr(clear));
  Register #(.width(16)) s0 (.D(write_value), .en(decoder_1_out8), .Q(s0_q), .clk(clock), .clr(clear));
  Register #(.width(16)) s2 (.D(write_value), .en(decoder_1_out10), .Q(s2_q), .clk(clock), .clr(clear));
  Register #(.width(16)) s4 (.D(write_value), .en(decoder_1_out12), .Q(s4_q), .clk(clock), .clr(clear));
  Register #(.width(16)) s6 (.D(write_value), .en(decoder_1_out14), .Q(s6_q), .clk(clock), .clr(clear));
  Register #(.width(16)) t1 (.D(write_value), .en(decoder_1_out1), .Q(t1_q), .clk(clock), .clr(clear));
  Register #(.width(16)) t3 (.D(write_value), .en(decoder_1_out3), .Q(t3_q), .clk(clock), .clr(clear));
  Register #(.width(16)) t5 (.D(write_value), .en(decoder_1_out5), .Q(t5_q), .clk(clock), .clr(clear));
  Register #(.width(16)) t7 (.D(write_value), .en(decoder_1_out7), .Q(t7_q), .clk(clock), .clr(clear));
  Register #(.width(16)) s1 (.D(write_value), .en(decoder_1_out9), .Q(s1_q), .clk(clock), .clr(clear));
  Register #(.width(16)) s3 (.D(write_value), .en(decoder_1_out11), .Q(s3_q), .clk(clock), .clr(clear));
  Register #(.width(16)) s5 (.D(write_value), .en(decoder_1_out13), .Q(s5_q), .clk(clock), .clr(clear));
  Register #(.width(16)) s7 (.D(write_value), .en(decoder_1_out15), .Q(s7_q), .clk(clock), .clr(clear));
  Multiplexer #(.select(4), .width(16)) multiplexer_1 (
    .in0({16{1'b0}}), .in1(t1_q), .in2(t2_q), .in3(t3_q), .in4(t4_q), .in5(t5_q), .in6(t6_q), .in7(t7_q),
    .in8(s0_q), .in9(s1_q), .in10(s2_q), .in11(s3_q), .in12(s4_q), .in13(s5_q), .in14(s6_q), .in15(s7_q),
    .out(Value_0), .sel(Read_0));  // open: en
  Multiplexer #(.select(4), .width(16)) multiplexer_2 (
    .in0({16{1'b0}}), .in1(t1_q), .in2(t2_q), .in3(t3_q), .in4(t4_q), .in5(t5_q), .in6(t6_q), .in7(t7_q),
    .in8(s0_q), .in9(s1_q), .in10(s2_q), .in11(s3_q), .in12(s4_q), .in13(s5_q), .in14(s6_q), .in15(s7_q),
    .out(Value_1), .sel(Read_1));  // open: en

  // Notes on the sheet:
  //   ADARSH CHAUDHARY    (1701CS01)
endmodule
