// Logisim project p1.circ as structural Verilog: 4 circuits, main circuit a
module a (
  input  Input,
  output Output
);

  wire and_1_out, and_2_out, clock_1_out, not_1_out, not_2_out, or_1_out;

  Clock clock_1 (.out(clock_1_out));
  not not_1 (not_1_out, Output);
  not not_2 (not_2_out, Input);
  D_Flip_Flop d_ff_1 (.clk(clock_1_out), .D(or_1_out), .Q(Output));  // open: Qn, preset, en, reset
  and and_1 (and_1_out, not_1_out, Input);
  and and_2 (and_2_out, Output, not_2_out);
  or or_1 (or_1_out, and_1_out, and_2_out);

  // Notes on the sheet:
  //   Adarsh Chaudhary  (1701CS01)
endmodule

module b (
  input  Input,
  output Output
);

  wire and_1_out, and_2_out, clock_1_out, not_1_out, not_2_out, not_3_out, or_1_out;

  Clock clock_1 (.out(clock_1_out));
  not not_1 (not_1_out, Output);
  not not_2 (not_2_out, Input);
  J_K_Flip_Flop j_k_ff_1 (.J(or_1_out), .clk(clock_1_out), .K(not_3_out), .Q(Output));  // open: Qn, preset, en, reset
  and and_1 (and_1_out, not_1_out, Input);
  and and_2 (and_2_out, Output, not_2_out);
  or or_1 (or_1_out, and_1_out, and_2_out);
  not not_3 (not_3_out, or_1_out);

  // Notes on the sheet:
  //   Adarsh Chaudhary  (1701CS01)
endmodule

module c (
  input  Input,
  output Output
);

  wire and_1_out, and_2_out, and_3_out, and_4_out, clock_1_out, not_1_out, not_2_out, not_3_out, not_4_out,
       or_1_out, or_2_out;

  Clock clock_1 (.out(clock_1_out));
  not not_1 (not_1_out, Output);
  not not_2 (not_2_out, or_2_out);
  not not_3 (not_3_out, Output);
  not not_4 (not_4_out, Input);
  T_Flip_Flop t_ff_1 (.clk(clock_1_out), .T(or_1_out), .Q(Output));  // open: Qn, preset, reset, en
  and and_1 (and_1_out, not_1_out, or_2_out);
  and and_2 (and_2_out, Output, not_2_out);
  and and_3 (and_3_out, not_3_out, Input);
  and and_4 (and_4_out, Output, not_4_out);
  or or_1 (or_1_out, and_1_out, and_2_out);
  or or_2 (or_2_out, and_3_out, and_4_out);

  // Notes on the sheet:
  //   Adarsh Chaudhary  (1701CS01)
endmodule

module d (
  input  Input,
  output Output
);

  wire and_1_out, and_2_out, and_3_out, and_4_out, clock_1_out, not_1_out, not_2_out, not_3_out, not_4_out,
       or_1_out;

  Clock clock_1 (.out(clock_1_out));
  not not_1 (not_1_out, Output);
  not not_2 (not_2_out, Output);
  not not_3 (not_3_out, Input);
  S_R_Flip_Flop s_r_ff_1 (.S(and_1_out), .clk(clock_1_out), .R(and_2_out), .Q(Output));  // open: Qn, preset, reset, en
  and and_1 (and_1_out, not_1_out, or_1_out);
  and and_2 (and_2_out, Output, not_4_out);
  not not_4 (not_4_out, or_1_out);
  and and_3 (and_3_out, not_2_out, Input);
  and and_4 (and_4_out, Output, not_3_out);
  or or_1 (or_1_out, and_3_out, and_4_out);

  // Notes on the sheet:
  //   Adarsh Chaudhary  (1701CS01)
endmodule
