// Logisim project p2.circ as structural Verilog: 2 circuits, main circuit a
module a (
  input  c0,
  input  c1,
  output n1,
  output n0,
  output o1,
  output o0
);

  wire and_1_out, and_2_out, and_3_out, and_4_out, and_5_out, and_6_out, and_7_out, and_8_out, and_9_out,
       and_10_out, and_11_out, and_12_out, and_13_out, and_14_out, and_15_out, and_16_out, clock_1_out,
       not_1_out, not_2_out, not_3_out, not_4_out, not_5_out, not_6_out, not_7_out, not_8_out, not_9_out,
       not_10_out, not_11_out, not_12_out, or_1_out, or_2_out, or_3_out, or_4_out;

  Clock clock_1 (.out(clock_1_out));
  not not_1 (not_1_out, c0);
  and and_1 (and_1_out, not_1_out, o1);
  not not_2 (not_2_out, o0);
  not not_3 (not_3_out, c1);
  and and_2 (and_2_out, not_3_out, o1);
  and and_3 (and_3_out, c1, not_4_out);
  not not_4 (not_4_out, o1);
  and and_4 (and_4_out, c0, not_5_out);
  not not_5 (not_5_out, o1);
  not not_6 (not_6_out, o0);
  not not_7 (not_7_out, c0);
  and and_5 (and_5_out, not_7_out, not_8_out);
  not not_8 (not_8_out, c1);
  not not_9 (not_9_out, c0);
  and and_6 (and_6_out, not_9_out, c1);
  not not_10 (not_10_out, o0);
  and and_7 (and_7_out, c0, not_11_out);
  not not_11 (not_11_out, c1);
  not not_12 (not_12_out, o0);
  and and_8 (and_8_out, c0, c1);
  D_Flip_Flop d_ff_1 (.clk(clock_1_out), .D(n1), .Q(o1));  // open: Qn, preset, en, reset
  and and_9 (and_9_out, and_1_out, not_2_out);
  and and_10 (and_10_out, and_2_out, o0);
  and and_11 (and_11_out, and_3_out, o0);
  and and_12 (and_12_out, and_4_out, not_6_out);
  and and_13 (and_13_out, and_5_out, o0);
  and and_14 (and_14_out, and_6_out, not_10_out);
  and and_15 (and_15_out, and_7_out, not_12_out);
  and and_16 (and_16_out, and_8_out, o0);
  D_Flip_Flop d_ff_2 (.clk(clock_1_out), .D(n0), .Q(o0));  // open: Qn, preset, en, reset
  or or_1 (or_1_out, and_9_out, and_10_out);
  or or_2 (or_2_out, and_11_out, and_12_out);
  or or_3 (or_3_out, and_13_out, and_14_out);
  or or_4 (or_4_out, and_15_out, and_16_out);
  or or_5 (n1, or_1_out, or_2_out);
  or or_6 (n0, or_3_out, or_4_out);

  // Notes on the sheet:
  //   Adarsh Chaudhary  (1701CS01)
endmodule

module b (
  input  c0,
  input  c1,
  output o1,
  output o0
);

  wire and_1_out, and_2_out, and_3_out, and_4_out, and_5_out, and_6_out, and_7_out, and_8_out, and_9_out,
       and_10_out, and_11_out, and_12_out, and_13_out, and_14_out, and_15_out, and_16_out, clock_1_out,
       not_1_out, not_2_out, not_3_out, not_4_out, not_5_out, not_6_out, not_7_out, not_8_out, not_9_out,
       not_10_out, not_11_out, not_12_out, not_13_out, not_14_out, or_1_out, or_2_out, or_3_out, or_4_out,
       or_5_out, or_6_out;

  Clock clock_1 (.out(clock_1_out));
  not not_1 (not_1_out, c0);
  and and_1 (and_1_out, not_1_out, o1);
  not not_2 (not_2_out, o0);
  not not_3 (not_3_out, c1);
  and and_2 (and_2_out, not_3_out, o1);
  and and_3 (and_3_out, c1, not_4_out);
  not not_4 (not_4_out, o1);
  and and_4 (and_4_out, c0, not_5_out);
  not not_5 (not_5_out, o1);
  not not_6 (not_6_out, o0);
  not not_7 (not_7_out, c0);
  and and_5 (and_5_out, not_7_out, not_8_out);
  not not_8 (not_8_out, c1);
  not not_9 (not_9_out, c0);
  and and_6 (and_6_out, not_9_out, c1);
  not not_10 (not_10_out, o0);
  and and_7 (and_7_out, c0, not_11_out);
  not not_11 (not_11_out, c1);
  not not_12 (not_12_out, o0);
  and and_8 (and_8_out, c0, c1);
  J_K_Flip_Flop j_k_ff_1 (.J(or_5_out), .clk(clock_1_out), .K(not_13_out), .Q(o1));  // open: Qn, preset, en, reset
  and and_9 (and_9_out, and_1_out, not_2_out);
  and and_10 (and_10_out, and_2_out, o0);
  and and_11 (and_11_out, and_3_out, o0);
  and and_12 (and_12_out, and_4_out, not_6_out);
  and and_13 (and_13_out, and_5_out, o0);
  and and_14 (and_14_out, and_6_out, not_10_out);
  and and_15 (and_15_out, and_7_out, not_12_out);
  and and_16 (and_16_out, and_8_out, o0);
  J_K_Flip_Flop j_k_ff_2 (.J(or_6_out), .clk(clock_1_out), .K(not_14_out), .Q(o0));  // open: Qn, preset, en, reset
  or or_1 (or_1_out, and_9_out, and_10_out);
  or or_2 (or_2_out, and_11_out, and_12_out);
  or or_3 (or_3_out, and_13_out, and_14_out);
  or or_4 (or_4_out, and_15_out, and_16_out);
  or or_5 (or_5_out, or_1_out, or_2_out);
  or or_6 (or_6_out, or_3_out, or_4_out);
  not not_13 (not_13_out, or_5_out);
  not not_14 (not_14_out, or_6_out);

  // Notes on the sheet:
  //   Adarsh Chaudhary  (1701CS01)
endmodule
