// Logisim project p3.circ as structural Verilog: 1 circuit, main circuit main
module main (
  input  [7:0] A,
  input  Load,
  input  [7:0] A_2,
  output [7:0] \output 
);

  wire adder_1_cout, adder_1_out, clock_1_out, d_ff_1_q, not_1_out, not_2_out, shift_register_1_out,
       shift_register_2_out;

  Clock clock_1 (.out(clock_1_out));
  not not_1 (not_1_out, Load);
  not not_2 (not_2_out, Load);
  Shift_Register shift_register_1 (
    .shift(not_1_out), .clk(clock_1_out), .out(shift_register_1_out), .load(Load), .d0(A[7]), .d1(A[6]),
    .d2(A[5]), .d3(A[4]), .d4(A[3]), .d5(A[2]), .d6(A[1]), .d7(A[0]));  // open: in, clr, q0, q1, q2, q3, q4, q5, q6, q7
  Shift_Register shift_register_2 (
    .shift(not_2_out), .clk(clock_1_out), .out(shift_register_2_out), .load(Load), .d0(A_2[7]), .d1(A_2[6]),
    .d2(A_2[5]), .d3(A_2[4]), .d4(A_2[3]), .d5(A_2[2]), .d6(A_2[1]), .d7(A_2[0]));  // open: in, clr, q0, q1, q2, q3, q4, q5, q6, q7
  D_Flip_Flop d_ff_1 (.clk(clock_1_out), .D(adder_1_cout), .Q(d_ff_1_q));  // open: Qn, preset, en, reset
  Adder #(.width(1)) adder_1 (
    .a(shift_register_1_out), .b(shift_register_2_out), .out(adder_1_out), .cin(d_ff_1_q), .cout(adder_1_cout));
  Shift_Register shift_register_3 (
    .in(adder_1_out), .clk(clock_1_out), .clr(Load), .q0(\output [7]), .q1(\output [6]), .q2(\output [5]),
    .q3(\output [4]), .q4(\output [3]), .q5(\output [2]), .q6(\output [1]), .q7(\output [0]));  // open: shift, out, load, d0, d1, d2, d3, d4, d5, d6, d7

  // Notes on the sheet:
  //   Adarsh Chaudhary  (1701CS01)
endmodule
