// Logisim project p4.circ as structural Verilog: 1 circuit, main circuit main
module main (
  input  clear,
  output [3:0] Satev
);

  wire clock_out;
  wire [3:0] multiplexer_1_out;

  Clock clock (.out(clock_out));
  Multiplexer #(.select(4), .width(4)) multiplexer_1 (
    .in0(4'b0001), .in1(4'b0100), .in2(4'b0101), .in3(4'b0100), .in4(4'b0000), .in5(4'b0000), .in6(4'b0111),
    .in7(4'b0000), .in8(4'b0000), .in9(4'b1010), .in10(4'b0000), .in11(4'b0000), .in12(4'b0000),
    .in13(4'b0000), .in14(4'b0000), .in15(4'b0000), .out(multiplexer_1_out), .sel(Satev));  // open: en
  Register #(.width(4)) register_1 (.D(multiplexer_1_out), .Q(Satev), .clk(clock_out), .clr(clear));  // open: en

  // Notes on the sheet:
  //   Adarsh Chaudhary  (1701CS01)
endmodule
