// Logisim project p5.circ as structural Verilog: 2 circuits, main circuit a
module a (
  output o2,
  output o1,
  output o0
);

  wire and_1_out, and_2_out, and_3_out, and_4_out, and_5_out, and_6_out, clock_1_out, not_1_out, not_2_out,
       not_3_out, not_4_out, not_5_out, not_6_out, or_1_out, or_2_out, or_3_out;

  Clock clock_1 (.out(clock_1_out));
  not not_1 (not_1_out, o2);
  not not_2 (not_2_out, o0);
  not not_3 (not_3_out, o2);
  not not_4 (not_4_out, o0);
  D_Flip_Flop d_ff_1 (.clk(clock_1_out), .D(or_3_out), .Q(o2));  // open: Qn, preset, en, reset
  and and_1 (and_1_out, not_1_out, o1);
  not not_5 (not_5_out, o0);
  not not_6 (not_6_out, o1);
  and and_2 (and_2_out, not_3_out, o1);
  and and_3 (and_3_out, o1, not_4_out);
  and and_4 (and_4_out, and_1_out, not_5_out);
  and and_5 (and_5_out, o2, not_6_out);
  or or_1 (or_1_out, and_2_out, and_3_out);
  D_Flip_Flop d_ff_2 (.clk(clock_1_out), .D(not_2_out), .Q(o1));  // open: Qn, preset, en, reset
  or or_2 (or_2_out, and_4_out, and_5_out);
  or or_3 (or_3_out, or_2_out, and_6_out);
  and and_6 (and_6_out, o2, o0);
  D_Flip_Flop d_ff_3 (.clk(clock_1_out), .D(or_1_out), .Q(o0));  // open: Qn, preset, en, reset

  // Notes on the sheet:
  //   Adarsh Chaudhary  (1701CS01)
endmodule

module b (
  output o2,
  output o1,
  output o0
);

  wire and_1_out, and_2_out, and_3_out, and_4_out, and_5_out, and_6_out, clock_1_out, not_1_out, not_2_out,
       not_3_out, not_4_out, not_5_out, not_6_out, not_7_out, not_8_out, not_9_out, or_1_out, or_2_out,
       or_3_out;

  Clock clock_1 (.out(clock_1_out));
  not not_1 (not_1_out, o2);
  not not_2 (not_2_out, o0);
  not not_3 (not_3_out, o2);
  not not_4 (not_4_out, o0);
  J_K_Flip_Flop j_k_ff_1 (.J(or_3_out), .clk(clock_1_out), .K(not_9_out), .Q(o2));  // open: Qn, preset, en, reset
  and and_1 (and_1_out, not_1_out, o1);
  not not_5 (not_5_out, o0);
  not not_6 (not_6_out, o1);
  and and_2 (and_2_out, not_3_out, o1);
  and and_3 (and_3_out, o1, not_4_out);
  and and_4 (and_4_out, and_1_out, not_5_out);
  and and_5 (and_5_out, o2, not_6_out);
  or or_1 (or_1_out, and_2_out, and_3_out);
  J_K_Flip_Flop j_k_ff_2 (.J(not_2_out), .clk(clock_1_out), .K(not_8_out), .Q(o1));  // open: Qn, preset, en, reset
  or or_2 (or_2_out, and_4_out, and_5_out);
  or or_3 (or_3_out, or_2_out, and_6_out);
  and and_6 (and_6_out, o2, o0);
  J_K_Flip_Flop j_k_ff_3 (.J(or_1_out), .clk(clock_1_out), .K(not_7_out), .Q(o0));  // open: Qn, preset, en, reset
  not not_7 (not_7_out, or_1_out);
  not not_8 (not_8_out, not_2_out);
  not not_9 (not_9_out, or_3_out);
endmodule
