// Logisim project p1.circ as structural Verilog: 1 circuit, main circuit main
module main (
  input  [7:0] in_1,
  input  in_2,
  input  [7:0] in_3,
  input  in_4,
  input  [7:0] in_5,
  input  in_6,
  output [7:0] out_7,
  output [7:0] out_8
);

  wire not_1_out;

  assign out_8 = in_4 ? in_3 : 8'bz;  // Controlled_Buffer controlled_buffer_1
  not not_1 (not_1_out, in_4);
  ROM rom_1 (.addr(in_1), .data(out_7), .sel(in_2));
  RAM #(.bus("asynch")) ram_1 (.addr(in_5), .data(out_8), .sel(in_6), .ld(not_1_out));  // open: clr

  // Notes on the sheet:
  //   ADARSH CHAUDHARY  (1701CS01)
  //   contents of rom_1 (hex, n*v repeats v):
  //   11 14*0 11 96*0 11 14*0 11
  //   ROM Implementation
  //   RAM Implementation
endmodule
