// Logisim project p2.circ as structural Verilog: 1 circuit, main circuit main
module main (
  input  [7:0] in_1,
  input  [7:0] in_2,
  input  [7:0] in_3,
  input  [7:0] in_4,
  input  in_5,
  input  [18:0] in_6,
  input  in_7,
  input  [1:0] in_8,
  output [7:0] out_9,
  output [7:0] out_10,
  output [7:0] out_11,
  output [7:0] out_12
);

  wire decoder_1_out0, decoder_1_out1, decoder_1_out2, decoder_1_out3, not_1_out, not_2_out, not_3_out,
       not_4_out;

  Decoder #(.select(2), .enable("false")) decoder_1 (
    .out0(decoder_1_out0), .out1(decoder_1_out1), .out2(decoder_1_out2), .out3(decoder_1_out3), .sel(in_8));
  assign out_12 = in_5 ? in_4 : 8'bz;  // Controlled_Buffer controlled_buffer_1
  assign out_11 = in_5 ? in_3 : 8'bz;  // Controlled_Buffer controlled_buffer_2
  assign out_10 = in_5 ? in_2 : 8'bz;  // Controlled_Buffer controlled_buffer_3
  assign out_9 = in_5 ? in_1 : 8'bz;  // Controlled_Buffer controlled_buffer_4
  not not_1 (not_1_out, in_5);
  not not_2 (not_2_out, in_5);
  not not_3 (not_3_out, in_5);
  RAM #(.addrWidth(19), .bus("asynch")) ram_1 (
    .addr(in_6), .data(out_9), .sel(decoder_1_out0), .ld(not_4_out), .clr(in_7));
  not not_4 (not_4_out, in_5);
  RAM #(.addrWidth(19), .bus("asynch")) ram_2 (
    .addr(in_6), .data(out_9), .sel(decoder_1_out1), .ld(not_4_out), .clr(in_7));
  RAM #(.addrWidth(19), .bus("asynch")) ram_3 (
    .addr(in_6), .data(out_9), .sel(decoder_1_out2), .ld(not_4_out), .clr(in_7));
  RAM #(.addrWidth(19), .bus("asynch")) ram_4 (
    .addr(in_6), .data(out_9), .sel(decoder_1_out3), .ld(not_4_out), .clr(in_7));
  RAM #(.addrWidth(19), .bus("asynch")) ram_5 (
    .addr(in_6), .data(out_10), .sel(decoder_1_out0), .ld(not_3_out), .clr(in_7));
  RAM #(.addrWidth(19), .bus("asynch")) ram_6 (
    .addr(in_6), .data(out_10), .sel(decoder_1_out1), .ld(not_3_out), .clr(in_7));
  RAM #(.addrWidth(19), .bus("asynch")) ram_7 (
    .addr(in_6), .data(out_10), .sel(decoder_1_out2), .ld(not_3_out), .clr(in_7));
  RAM #(.addrWidth(19), .bus("asynch")) ram_8 (
    .addr(in_6), .data(out_10), .sel(decoder_1_out3), .ld(not_3_out), .clr(in_7));
  RAM #(.addrWidth(19), .bus("asynch")) ram_9 (
    .addr(in_6), .data(out_11), .sel(decoder_1_out0), .ld(not_2_out), .clr(in_7));
  RAM #(.addrWidth(19), .bus("asynch")) ram_10 (
    .addr(in_6), .data(out_11), .sel(decoder_1_out1), .ld(not_2_out), .clr(in_7));
  RAM #(.addrWidth(19), .bus("asynch")) ram_11 (
    .addr(in_6), .data(out_11), .sel(decoder_1_out2), .ld(not_2_out), .clr(in_7));
  RAM #(.addrWidth(19), .bus("asynch")) ram_12 (
    .addr(in_6), .data(out_11), .sel(decoder_1_out3), .ld(not_2_out), .clr(in_7));
  RAM #(.addrWidth(19), .bus("asynch")) ram_13 (
    .addr(in_6), .data(out_12), .sel(decoder_1_out0), .ld(not_1_out), .clr(in_7));
  RAM #(.addrWidth(19), .bus("asynch")) ram_14 (
    .addr(in_6), .data(out_12), .sel(decoder_1_out1), .ld(not_1_out), .clr(in_7));
  RAM #(.addrWidth(19), .bus("asynch")) ram_15 (
    .addr(in_6), .data(out_12), .sel(decoder_1_out2), .ld(not_1_out), .clr(in_7));
  RAM #(.addrWidth(19), .bus("asynch")) ram_16 (
    .data(out_12), .sel(decoder_1_out3), .ld(not_1_out), .clr(in_7));  // open: addr

  // Notes on the sheet:
  //                                      2M * 32 Memory using 16 512K * 8 memory chips 
  //   ADARSH CHAUDHARY (1701CS01)
endmodule
