// Logisim project p3.circ as structural Verilog: 1 circuit, main circuit main
module main (
  input  in_1
);

  wire clock_1_out;
  wire [23:0] counter_1_q;
  wire [31:0] rom_1_data;

  Counter #(.width(24), .max('hffffff)) counter_1 (
    .Q(counter_1_q), .clk(clock_1_out), .clr(in_1));  // open: load, D, count, carry
  Clock clock_1 (.out(clock_1_out));
  ROM #(.addrWidth(24), .dataWidth(32)) rom_1 (.addr(counter_1_q), .data(rom_1_data));  // open: sel
  Hex_Digit_Display hex_digit_display_1 (.value(rom_1_data[31:28]));  // open: dp
  Hex_Digit_Display hex_digit_display_2 (.value(rom_1_data[27:24]));  // open: dp
  Hex_Digit_Display hex_digit_display_3 (.value(rom_1_data[19:16]));  // open: dp
  Hex_Digit_Display hex_digit_display_4 (.value(rom_1_data[23:20]));  // open: dp
  Hex_Digit_Display hex_digit_display_5 (.value(rom_1_data[15:12]));  // open: dp
  Hex_Digit_Display hex_digit_display_6 (.value(rom_1_data[11:8]));  // open: dp
  Hex_Digit_Display hex_digit_display_7 (.value(rom_1_data[7:4]));  // open: dp
  Hex_Digit_Display hex_digit_display_8 (.value(rom_1_data[3:0]));  // open: dp

  // Notes on the sheet:
  //   contents of rom_1 (hex, n*v repeats v):
  //   20020005 2003000c 2067fff7 e22025 642824 a42820 10a7000a 64202a 10800001 20050000 e2202a 853820
  //   e23822 ac670044 8c020050 8000011 20020001 ac020054
  //   ADARSH CHAUDHARY (1701CS01)
endmodule
