// Logisim project p4.circ as structural Verilog: 2 circuits, main circuit main
module main (
  input  i2,
  input  i3,
  input  in_3,
  input  i4,
  input  i1,
  input  i0,
  input  i5,
  input  i7,
  input  i6,
  input  [23:0] position,
  input  write,
  input  [2:0] position1
);

  wire decoder_1_out0, decoder_1_out2, decoder_1_out3, decoder_1_out4, decoder_1_out5, decoder_1_out6,
       decoder_1_out7;

  Decoder #(.select(3), .enable("false")) decoder_1 (
    .out0(decoder_1_out0), .out1(i0), .out2(decoder_1_out2), .out3(decoder_1_out3), .out4(decoder_1_out4),
    .out5(decoder_1_out5), .out6(decoder_1_out6), .out7(decoder_1_out7), .sel(position1));
  _8_bit u_8_bit_1 (
    .i1(i1), .i0(i0), .i5(i5), .i4(i4), .i3(i3), .i2(i2), .i7(i7), .i6(i6), .write(write),
    .sel(decoder_1_out0), .position(position));  // open: o7, o6, o5, o4, o3, o2, o1, o0
  _8_bit u_8_bit_2 (
    .i1(i1), .i0(i0), .i5(i5), .i4(i4), .i3(i3), .i2(i2), .i7(i7), .i6(i6), .write(i6), .sel(i0),
    .position(position));  // open: o7, o6, o5, o4, o3, o2, o1, o0
  _8_bit u_8_bit_3 (
    .i1(i1), .i5(i5), .i4(i4), .i3(i3), .i2(i2), .i7(i7), .sel(decoder_1_out2), .position(position));  // open: i0, i6, write, o7, o6, o5, o4, o3, o2, o1, o0
  _8_bit u_8_bit_4 (
    .sel(decoder_1_out3), .position(position));  // open: i1, i0, i5, i4, i3, i2, i7, i6, write, o7, o6, o5, o4, o3, o2, o1, o0
  _8_bit u_8_bit_5 (
    .sel(decoder_1_out4), .position(position));  // open: i1, i0, i5, i4, i3, i2, i7, i6, write, o7, o6, o5, o4, o3, o2, o1, o0
  _8_bit u_8_bit_6 (
    .sel(decoder_1_out5), .position(position));  // open: i1, i0, i5, i4, i3, i2, i7, i6, write, o7, o6, o5, o4, o3, o2, o1, o0
  _8_bit u_8_bit_7 (
    .sel(decoder_1_out6), .position(position));  // open: i1, i0, i5, i4, i3, i2, i7, i6, write, o7, o6, o5, o4, o3, o2, o1, o0
  _8_bit u_8_bit_8 (
    .sel(decoder_1_out7), .position(position));  // open: i1, i0, i5, i4, i3, i2, i7, i6, write, o7, o6, o5, o4, o3, o2, o1, o0

  // Notes on the sheet:
  //   ADARSH CHAUDHARY (1701CS01)
endmodule

module _8_bit (
  input  i1,
  input  i0,
  input  i5,
  input  i4,
  input  i3,
  input  i2,
  input  i7,
  input  i6,
  input  write,
  input  sel,
  input  [23:0] position,
  output o1,
  output o0,
  output o5,
  output o4,
  output o3,
  output o2,
  output o7,
  output o6
);

  wire not_1_out, not_2_out, not_3_out, not_4_out, not_5_out, not_6_out, not_7_out, not_8_out;

  assign o7 = write ? i7 : 1'bz;  // Controlled_Buffer controlled_buffer_1
  not not_1 (not_1_out, write);
  RAM #(.addrWidth(24), .dataWidth(1), .bus("asynch")) ram_1 (
    .addr(position), .data(o7), .sel(sel), .ld(not_1_out));  // open: clr
  assign o6 = write ? i6 : 1'bz;  // Controlled_Buffer controlled_buffer_2
  not not_2 (not_2_out, write);
  assign o5 = write ? i5 : 1'bz;  // Controlled_Buffer controlled_buffer_3
  RAM #(.addrWidth(24), .dataWidth(1), .bus("asynch")) ram_2 (
    .addr(position), .data(o6), .sel(sel), .ld(not_2_out));  // open: clr
  not not_3 (not_3_out, write);
  RAM #(.addrWidth(24), .dataWidth(1), .bus("asynch")) ram_3 (
    .addr(position), .data(o5), .sel(sel), .ld(not_3_out));  // open: clr
  assign o4 = write ? i4 : 1'bz;  // Controlled_Buffer controlled_buffer_4
  not not_4 (not_4_out, write);
  RAM #(.addrWidth(24), .dataWidth(1), .bus("asynch")) ram_4 (
    .addr(position), .data(o4), .sel(sel), .ld(not_4_out));  // open: clr
  assign o3 = write ? i3 : 1'bz;  // Controlled_Buffer controlled_buffer_5
  not not_5 (not_5_out, write);
  RAM #(.addrWidth(24), .dataWidth(1), .bus("asynch")) ram_5 (
    .addr(position), .data(o3), .sel(sel), .ld(not_5_out));  // open: clr
  assign o2 = write ? i2 : 1'bz;  // Controlled_Buffer controlled_buffer_6
  not not_6 (not_6_out, write);
  assign o1 = write ? i1 : 1'bz;  // Controlled_Buffer controlled_buffer_7
  not not_7 (not_7_out, write);
  RAM #(.addrWidth(24), .dataWidth(1), .bus("asynch")) ram_6 (
    .addr(position), .data(o2), .sel(sel), .ld(not_6_out));  // open: clr
  RAM #(.addrWidth(24), .dataWidth(1), .bus("asynch")) ram_7 (
    .addr(position), .data(o1), .sel(sel), .ld(not_7_out));  // open: clr
  assign o0 = write ? i0 : 1'bz;  // Controlled_Buffer controlled_buffer_8
  not not_8 (not_8_out, write);
  RAM #(.addrWidth(24), .dataWidth(1), .bus("asynch")) ram_8 (
    .addr(position), .data(o0), .sel(sel), .ld(not_8_out));  // open: clr
endmodule
