// Logisim project p5.circ as structural Verilog: 1 circuit, main circuit main
module main (
);

  wire Clock_out, not_1_out, Write_out;
  wire [6:0] controlled_buffer_1_out, Data_out;
  wire [19:0] Address_out;

  Clock Clock (.out(Clock_out));
  Random #(.width(7)) Data (.clk(Clock_out), .next(1'b1), .out(Data_out));  // open: clr
  Random #(.width(20)) Address (.clk(Clock_out), .next(1'b1), .out(Address_out));  // open: clr
  Random #(.width(1), .seed(5)) Write (.clk(Clock_out), .next(1'b1), .out(Write_out));  // open: clr
  assign controlled_buffer_1_out = Write_out ? Data_out : 7'bz;  // Controlled_Buffer controlled_buffer_1
  not not_1 (not_1_out, Write_out);
  RAM #(.addrWidth(20), .dataWidth(7)) ram_1 (
    .addr(Address_out), .data(controlled_buffer_1_out), .sel(1'b1), .clk(Clock_out), .ld(not_1_out));  // open: clr
  TTY tty_1 (.data(controlled_buffer_1_out), .clk(Clock_out));  // open: we, clr

  // Notes on the sheet:
  //   ADARSH CHAUDHARY (1701CS01)
endmodule
