// Logisim project p1.circ as structural Verilog: 1 circuit, main circuit main
module main (
  input  A,
  input  A_2,
  input  B,
  input  B_2,
  input  C,
  input  C_2,
  input  D,
  input  D_2,
  output out_9,
  output out_10,
  output out_11,
  output out_12,
  output out_13,
  output out_14,
  output out_15,
  output out_16
);

  Transistor transistor_1 (.in(1'b1), .out(out_10), .gate(A));
  Transistor transistor_2 (.in(out_10), .out(out_12), .gate(B));
  Transistor transistor_3 (.in(out_12), .out(out_14), .gate(C));
  Transistor transistor_4 (.in(out_14), .out(out_16), .gate(D));
  Transistor #(.\type ("n")) transistor_5 (.in(out_11), .out(out_9), .gate(A_2));
  Transistor #(.\type ("n")) transistor_6 (.in(out_13), .out(out_11), .gate(B_2));
  Transistor #(.\type ("n")) transistor_7 (.in(out_15), .out(out_13), .gate(C_2));
  Transistor #(.\type ("n")) transistor_8 (.in(1'b0), .out(out_15), .gate(D_2));

  // Notes on the sheet:
  //   Name: Adarsh Chaudhary
  //   Rollno: 1701CS01
endmodule
