// Logisim project p2.circ as structural Verilog: 4 circuits, main circuit NAND
module NAND (
  input  A,
  input  B,
  input  C,
  input  D,
  input  E,
  output OUTPUT
);

  wire transistor_2_out, transistor_3_out, transistor_4_out, transistor_5_out;

  Pull_Resistor #(.pull(1)) pull_resistor_1 (.node(OUTPUT));
  Transistor #(.\type ("n")) transistor_1 (.in(transistor_2_out), .out(OUTPUT), .gate(A));
  Transistor #(.\type ("n")) transistor_2 (.in(transistor_3_out), .out(transistor_2_out), .gate(B));
  Transistor #(.\type ("n")) transistor_3 (.in(transistor_4_out), .out(transistor_3_out), .gate(C));
  Transistor #(.\type ("n")) transistor_4 (.in(transistor_5_out), .out(transistor_4_out), .gate(D));
  Transistor #(.\type ("n")) transistor_5 (.in(1'b0), .out(transistor_5_out), .gate(E));

  // Notes on the sheet:
  //   Name: Adarsh Chaudhary
  //   Rollno: 1701CS01
  //   GND
endmodule

module NOR (
  input  in_1,
  input  in_2,
  input  in_3,
  input  in_4,
  input  in_5,
  output OUTPUT
);

  Pull_Resistor #(.pull(1)) pull_resistor_1 (.node(OUTPUT));
  Transistor #(.\type ("n")) transistor_1 (.in(1'b0), .out(OUTPUT), .gate(in_1));
  Transistor #(.\type ("n")) transistor_2 (.in(1'b0), .out(OUTPUT), .gate(in_2));
  Transistor #(.\type ("n")) transistor_3 (.in(1'b0), .out(OUTPUT), .gate(in_3));
  Transistor #(.\type ("n")) transistor_4 (.in(1'b0), .out(OUTPUT), .gate(in_5));
  Transistor #(.\type ("n")) transistor_5 (.in(1'b0), .out(OUTPUT), .gate(in_4));

  // Notes on the sheet:
  //   Name: Adarsh Chaudhary
  //   Rollno: 1701CS01
  //   GND
endmodule

module AND (
  input  A,
  input  B,
  input  C,
  input  D,
  input  E,
  output out_6
);

  wire pull_resistor_1_node, transistor_2_out, transistor_3_out, transistor_4_out, transistor_5_out;

  Pull_Resistor #(.pull(1)) pull_resistor_1 (.node(pull_resistor_1_node));
  Transistor #(.\type ("n")) transistor_1 (.in(transistor_2_out), .out(pull_resistor_1_node), .gate(A));
  Transistor #(.\type ("n")) transistor_2 (.in(transistor_3_out), .out(transistor_2_out), .gate(B));
  Transistor #(.\type ("n")) transistor_3 (.in(transistor_4_out), .out(transistor_3_out), .gate(C));
  Transistor #(.\type ("n")) transistor_4 (.in(transistor_5_out), .out(transistor_4_out), .gate(D));
  Transistor #(.\type ("n")) transistor_5 (.in(1'b0), .out(transistor_5_out), .gate(E));
  Pull_Resistor #(.pull(1)) pull_resistor_2 (.node(out_6));
  Transistor #(.\type ("n")) transistor_6 (.in(1'b0), .out(out_6), .gate(pull_resistor_1_node));

  // Notes on the sheet:
  //   Name: Adarsh Chaudhary
  //   Rollno: 1701CS01
  //   GND
  //   OUTPUT
  //   GND
endmodule

module OR (
  input  A,
  input  B,
  input  C,
  input  D,
  input  E,
  output OUTPUT
);

  wire pull_resistor_1_node;

  Pull_Resistor #(.pull(1)) pull_resistor_1 (.node(pull_resistor_1_node));
  Transistor #(.\type ("n")) transistor_1 (.in(1'b0), .out(pull_resistor_1_node), .gate(A));
  Transistor #(.\type ("n")) transistor_2 (.in(1'b0), .out(pull_resistor_1_node), .gate(B));
  Transistor #(.\type ("n")) transistor_3 (.in(1'b0), .out(pull_resistor_1_node), .gate(D));
  Transistor #(.\type ("n")) transistor_4 (.in(1'b0), .out(pull_resistor_1_node), .gate(C));
  Transistor #(.\type ("n")) transistor_5 (.in(1'b0), .out(pull_resistor_1_node), .gate(E));
  Pull_Resistor #(.pull(1)) pull_resistor_2 (.node(OUTPUT));
  Transistor #(.\type ("n")) transistor_6 (.in(1'b0), .out(OUTPUT), .gate(pull_resistor_1_node));

  // Notes on the sheet:
  //   Name: Adarsh Chaudhary
  //   Rollno: 1701CS01
  //   GND
endmodule
