// Logisim project p3.circ as structural Verilog: 1 circuit, main circuit main
module main (
  input  A,
  input  B,
  input  C,
  input  D,
  input  E,
  output out_6
);

  wire transistor_1_out, transistor_2_out, transistor_3_out, transistor_5_out, transistor_9_out;

  Transistor transistor_1 (.in(1'b1), .out(transistor_1_out), .gate(A));
  Transistor transistor_2 (.in(transistor_1_out), .out(transistor_2_out), .gate(C));
  Transistor transistor_3 (.in(transistor_2_out), .out(transistor_3_out), .gate(E));
  Transistor #(.\type ("n")) transistor_4 (.in(transistor_5_out), .out(transistor_3_out), .gate(A));
  Transistor #(.\type ("n")) transistor_5 (.in(1'b0), .out(transistor_5_out), .gate(B));
  Transistor transistor_6 (.in(1'b1), .out(transistor_1_out), .gate(B));
  Transistor transistor_7 (.in(transistor_1_out), .out(transistor_2_out), .gate(D));
  Transistor #(.\type ("n")) transistor_8 (.in(transistor_9_out), .out(transistor_3_out), .gate(C));
  Transistor #(.\type ("n")) transistor_9 (.in(1'b0), .out(transistor_9_out), .gate(D));
  Transistor #(.\type ("n")) transistor_10 (.in(1'b0), .out(transistor_3_out), .gate(E));
  Transistor transistor_11 (.in(1'b1), .out(out_6), .gate(transistor_3_out));
  Transistor #(.\type ("n")) transistor_12 (.in(1'b0), .out(out_6), .gate(transistor_3_out));

  // Notes on the sheet:
  //   Name: Adarsh Chaudhary
  //   Rollno: 1701CS01
  //   GND
endmodule
