// Logisim project p3.circ as structural Verilog: 3 circuits, main circuit 2-1 multiplexer
module _4_1_multiplexer (
  input  in_1,
  input  in_2,
  input  in_3,
  input  in_4,
  input  in_5,
  input  in_6,
  output out_7
);

  wire and_1_out, and_2_out, and_3_out, and_4_out, not_1_out, not_2_out;

  not not_1 (not_1_out, in_5);
  not not_2 (not_2_out, in_6);
  and and_1 (and_1_out, in_1, not_1_out, not_2_out);
  and and_2 (and_2_out, in_2, not_1_out, in_6);
  and and_3 (and_3_out, in_3, in_5, not_2_out);
  and and_4 (and_4_out, in_4, in_5, in_6);
  or or_1 (out_7, and_1_out, and_2_out, and_3_out, and_4_out);
endmodule

module _2_1_multiplexer (
  input  I0,
  input  I1,
  input  S0,
  output Y
);

  wire and_1_out, and_2_out, not_1_out;

  not not_1 (not_1_out, S0);
  and and_1 (and_1_out, I0, not_1_out);
  and and_2 (and_2_out, I1, S0);
  or or_1 (Y, and_1_out, and_2_out);
endmodule

module \new  (
  input  in_1,
  input  in_2,
  input  in_3,
  input  in_4,
  input  in_5,
  input  in_6,
  input  in_7,
  input  in_8,
  input  in_9,
  output out_10,
  output out_11,
  output out_12,
  output out_13
);

  _2_1_multiplexer u_2_1_multiplexer_1 (.I0(in_1), .I1(in_2), .S0(in_9), .Y(out_10));
  _2_1_multiplexer u_2_1_multiplexer_2 (.I0(in_3), .I1(in_4), .S0(in_9), .Y(out_11));
  _2_1_multiplexer u_2_1_multiplexer_3 (.I0(in_5), .I1(in_6), .S0(in_9), .Y(out_12));
  _2_1_multiplexer u_2_1_multiplexer_4 (.I0(in_7), .I1(in_8), .S0(in_9), .Y(out_13));
endmodule
