// Logisim project p4.circ as structural Verilog: 3 circuits, main circuit Main
module Main (
  input  D,
  input  C,
  input  B,
  input  A,
  input  S3,
  input  S2,
  input  S1,
  input  S0,
  output O
);

  wire block_a_1_t0, block_a_1_t1;

  Block_A block_a_1 (.s0(S3), .s1(S2), .s2(S1), .s3(S0), .t0(block_a_1_t0), .t1(block_a_1_t1));
  Block_B block_b_1 (.in_1(A), .in_2(B), .in_3(C), .in_4(D), .in_5(block_a_1_t0), .in_6(block_a_1_t1), .out_7(O));
endmodule

// A
module Block_A (
  input  s0,
  input  s1,
  input  s2,
  input  s3,
  output t0,
  output t1
);

  wire not_1_out, not_2_out, not_3_out, not_4_out;

  not not_1 (not_1_out, s2);
  not not_2 (not_2_out, s3);
  not not_3 (not_3_out, s1);
  not not_4 (not_4_out, s3);
  and and_1 (t0, not_1_out, not_2_out);
  and and_2 (t1, not_3_out, not_4_out);
endmodule

// B
module Block_B (
  input  in_1,
  input  in_2,
  input  in_3,
  input  in_4,
  input  in_5,
  input  in_6,
  output out_7
);

  wire and_1_out, and_2_out, and_3_out, and_4_out, not_1_out, not_2_out;

  not not_1 (not_1_out, in_5);
  not not_2 (not_2_out, in_6);
  and and_1 (and_1_out, in_1, not_1_out, not_2_out);
  and and_2 (and_2_out, in_2, not_1_out, in_6);
  and and_3 (and_3_out, in_3, in_5, not_2_out);
  and and_4 (and_4_out, in_4, in_5, in_6);
  or or_1 (out_7, and_1_out, and_2_out, and_3_out, and_4_out);
endmodule
