// Logisim project p1.circ as structural Verilog: 1 circuit, main circuit main
module main (
  input  C_in,
  input  [1:0] A,
  output Sum,
  output C_out
);

  wire not_1_out;

  not not_1 (not_1_out, C_in);
  Multiplexer #(.select(2), .enable("false")) multiplexer_1 (
    .in0(C_in), .in1(not_1_out), .in2(not_1_out), .in3(C_in), .out(Sum), .sel(A));
  Multiplexer #(.select(2), .enable("false")) multiplexer_2 (
    .in0(1'b0), .in1(C_in), .in2(C_in), .in3(1'b1), .out(C_out), .sel(A));

  // Notes on the sheet:
  //   Adarsh Chaudhary   (1701CS01)
endmodule
