// Logisim project p3.circ as structural Verilog: 1 circuit, main circuit main
module main (
  input  in_1,
  input  [1:0] C_D,
  output Testing,
  output Y
);

  Multiplexer #(.select(2), .enable("false")) multiplexer_1 (
    .in0(in_1), .in1(1'b0), .in2(1'b0), .in3(in_1), .out(Testing), .sel(C_D));
  Multiplexer #(.enable("false")) multiplexer_2 (.in0(Testing), .in1(1'b1), .out(Y), .sel(1'b1));
endmodule
