// Logisim project p4.circ as structural Verilog: 3 circuits, main circuit 4a
module _4a (
  input  [2:0] A_B_C,
  output Output
);

  Multiplexer #(.select(3), .enable("false")) multiplexer_1 (
    .in0(1'b1), .in1(1'b0), .in2(1'b0), .in3(1'b0), .in4(1'b0), .in5(1'b0), .in6(1'b0), .in7(1'b1),
    .out(Output), .sel(A_B_C));

  // Notes on the sheet:
  //   Adarsh Chaudhary   (1701CS01)
endmodule

module _4b (
  input  C,
  input  [1:0] A_B,
  output Output
);

  wire not_1_out;

  not not_1 (not_1_out, C);
  Multiplexer #(.select(2), .enable("false")) multiplexer_1 (
    .in0(not_1_out), .in1(1'b0), .in2(1'b0), .in3(C), .out(Output), .sel(A_B));

  // Notes on the sheet:
  //   Adarsh Chaudhary   (1701CS01)
endmodule

module _4c (
  input  A,
  input  B,
  input  C,
  output Output
);

  wire and_1_out, nor_1_out;

  nor nor_1 (nor_1_out, A, B, C);
  and and_1 (and_1_out, A, B, C);
  Multiplexer #(.enable("false")) multiplexer_1 (.in0(nor_1_out), .in1(C), .out(Output), .sel(and_1_out));

  // Notes on the sheet:
  //   Adarsh Chaudhary   (1701CS01)
endmodule
