// Logisim project p5.circ as structural Verilog: 1 circuit, main circuit main
module main (
  input  A0,
  input  A1,
  input  A2,
  input  A3,
  output Y1,
  output Y2,
  output Y3,
  output Y3_2
);

  wire not_1_out, not_2_out, not_3_out;

  not not_1 (not_1_out, A1);
  not not_2 (not_2_out, A2);
  not not_3 (not_3_out, A3);
  and and_1 (Y1, A0, not_1_out, not_2_out, not_3_out);
  and and_2 (Y2, A1, not_2_out, not_3_out);
  and and_3 (Y3, A2, not_3_out);

  assign Y3_2 = A3;

  // Notes on the sheet:
  //   Adarsh Chaudhary   (1701CS01)
endmodule
