// Logisim project p3.circ as structural Verilog: 1 circuit, main circuit main
module main (
  input  I0,
  input  I1,
  input  I2,
  input  I3,
  input  in_5,
  input  [1:0] S,
  input  shr_in,
  output out_8,
  output out_9,
  output out_10,
  output out_11
);

  wire clock_1_out, multiplexer_1_out, multiplexer_2_out, multiplexer_3_out, multiplexer_4_out;

  Clock clock_1 (.out(clock_1_out));
  Multiplexer #(.select(2), .enable("false")) multiplexer_1 (
    .in0(out_8), .in1(I0), .in2(out_9), .in3(1'b0), .out(multiplexer_1_out), .sel(S));
  Multiplexer #(.select(2), .enable("false")) multiplexer_2 (
    .in0(out_9), .in1(I1), .in2(out_10), .in3(1'b0), .out(multiplexer_2_out), .sel(S));
  Multiplexer #(.select(2), .enable("false")) multiplexer_3 (
    .in0(out_10), .in1(I2), .in2(out_11), .in3(1'b0), .out(multiplexer_3_out), .sel(S));
  Multiplexer #(.select(2), .enable("false")) multiplexer_4 (
    .in0(out_11), .in1(I3), .in2(shr_in), .in3(1'b0), .out(multiplexer_4_out), .sel(S));
  Register #(.width(1)) register_1 (.D(multiplexer_1_out), .en(in_5), .Q(out_8), .clk(clock_1_out));  // open: clr
  Register #(.width(1)) register_2 (.D(multiplexer_2_out), .en(in_5), .Q(out_9), .clk(clock_1_out));  // open: clr
  Register #(.width(1)) register_3 (.D(multiplexer_3_out), .en(in_5), .Q(out_10), .clk(clock_1_out));  // open: clr
  Register #(.width(1)) register_4 (.D(multiplexer_4_out), .en(in_5), .Q(out_11), .clk(clock_1_out));  // open: clr

  // Notes on the sheet:
  //   ADARSH CHAUDHARY    (1701CS01)
  //   Upward == Right
endmodule
